# Fritzing sketch PLACA_MODULO PISCINA (saved by Fritzing 1.0.1rc)
circuit board: 12.1cm x 8.5cm
breadboards: 3

parts:
  12V = Power Jack [package=power_jack_pth_lock]
  C1E = Capacitor Polarized [package=cpol-radial-100uf-25v]
  C1 = Ceramic Capacitor [capacitance=1µF voltage=35V package="200 mil [THT, multilayer]"]
  C2 = Ceramic Capacitor [capacitance=1µF voltage=35V package="200 mil [THT, multilayer]"]
  C2E = Capacitor Polarized [package=cpol-radial-100uf-25v]
  LED1 = LED - 5mm [color="Red (633nm)" current=0.030A package="5 mm [THT]"]
  R1 = Resistor [tolerance=±5% resistance=220 package=THT]
  R2 = Resistor [tolerance=±5% resistance=220 power=0.25W package=THT]
  J1 = Camdenboss CTB0158-11 [part_number=CTB0158-11 package=THT]
  R3 = Resistor [tolerance=±5% resistance=220 power=0.25W package=THT]
  R4 = Resistor [tolerance=±5% power=0.25W resistance=0 package=THT]
  R5 = Resistor [tolerance=±5% resistance=0 power=0.25W package=THT]
  J2 = Camdenboss CTB0158-2 [part_number=CTB0158-2 package=THT]
  LED2 = LED - 5mm [color="Red (633nm)" current=0.030A package="5 mm [THT]"]
  R6 = Resistor [tolerance=±5% resistance=0 power=0.25W package=THT]
  TIP122 = Voltage Regulator [package=to-220-alt]
  R7 = Resistor [tolerance=±5% resistance=220 power=0.25W package=THT]
  R8 = Resistor [tolerance=±5% resistance=0 power=0.25W package=THT]
  R9 = Resistor [tolerance=±5% resistance=0 power=0.25W package=THT]
  R10 = Resistor [tolerance=±5% resistance=0 power=0.25W package=THT]
  R11 = Resistor [tolerance=±5% resistance=0 power=0.25W package=THT]
  R12 = Resistor [tolerance=±5% resistance=0 power=0.25W package=THT]
  R13 = Resistor [tolerance=±5% resistance=0 power=0.25W package=THT]
  R14 = Resistor [tolerance=±5% resistance=0 power=0.25W package=THT]
  R15 = Resistor [tolerance=±5% resistance=0 power=0.25W package=THT]
  R16 = Resistor [tolerance=±5% resistance=0 power=0.25W package=THT]
  R18 = Resistor [tolerance=±5% resistance=0 power=0.25W package=THT]
  R19 = Resistor [tolerance=±5% resistance=0 power=0.25W package=THT]
  R20 = Resistor [tolerance=±5% resistance=0 power=0.25W package=THT]
  R22 = Resistor [tolerance=±5% resistance=0 power=0.25W package=THT]
  R23 = Resistor [tolerance=±5% resistance=0 power=0.25W package=THT]
  J3 = female pin header, 10 pins [form="♀ (female)"]  # not connected
  J4 = female pin header, 10 pins [form="♀ (female)"]
  J5 = female pin header, 10 pins [form="♀ (female)"]
  J6 = female pin header, 10 pins [form="♀ (female)"]  # not connected
  J7 = female pin header, 10 pins [form="♀ (female)"]
  LED3 = LED - 5mm [color="Red (633nm)" current=0.030A package="5 mm [THT]"]
  R24 = Resistor [tolerance=±5% resistance=0 power=0.25W package=THT]
  R25 = Resistor [tolerance=±5% resistance=0 power=0.25W package=THT]
  J9 = female pin header, 10 pins [form="♀ (female)"]  # not connected
  J10 = female pin header, 10 pins [form="♀ (female)"]  # not connected
  U1 = LuaNode32 / ESP32 [part_number=ESP32S-PIN30]
  7805 = Voltage Regulator [package=to-220-alt]
  R26 = Rotary Potentiometer (Large) [maximum_resistance=100kΩ knob_status=50% power=0.5W package=THT]
  R27 = Resistor [tolerance=±5% resistance=0 power=0.25W package=THT]

nets:
  GND: 12V.GND, C1E.-, C1.1, C2.0, C2E.-, R1.Pin_1, R2.Pin_1, J1.pin4, J1.pin6, J1.pin7, TIP122.OUT, R24.Pin_1, U1.GND, 7805.GND, R26.leg1
  N1: 12V.PWR, C1E.+, C1.0, R4.Pin_0, 7805.IN
  N2: C2.1, C2E.+, LED1.anode, U1.Vin, 7805.OUT
  N3: LED1.cathode, R1.Pin_0
  N4: R2.Pin_0, J1.pin11, U1.D14
  N5: J1.pin1, J1.pin2, J1.pin5, J1.pin8, J1.pin10, R5.Pin_1, LED2.cathode, R26.leg2
  N6: J1.pin3, R8.Pin_1
  N7: J1.pin9, R7.Pin_0
  N8: R3.Pin_0, TIP122.IN
  N9: R3.Pin_1, U1.D4
  N10: R4.Pin_1, J2.pin1
  N11: R5.Pin_0, U1.3V3
  N12: J2.pin2, R6.Pin_1, TIP122.GND
  N13: LED2.anode, R6.Pin_0
  N14: R7.Pin_1, U1.D15
  N15: R8.Pin_0, R9.Pin_1
  N16: R9.Pin_0, R16.Pin_0, U1.D32
  N17: R10.Pin_0, U1.D34
  N18: R11.Pin_0, U1.D35
  N19: R12.Pin_0, U1.D33
  N20: R13.Pin_0, U1.D25
  N21: R14.Pin_0, U1.D26
  N22: R15.Pin_0, U1.VN
  N23: R18.Pin_0, U1.D18
  N24: R19.Pin_0, U1.D19
  N25: R20.Pin_0, U1.D22
  N26: R22.Pin_0, U1.D23
  N27: R23.Pin_0, U1.D21
  N28: J4.pin10, U1.D13
  N29: J5.pin10, U1.D12
  N30: J7.pin10, U1.D27
  N31: LED3.cathode, R25.Pin_0
  N32: LED3.anode, R24.Pin_0
  N33: R25.Pin_1, U1.D2
  N34: U1.D5, R27.Pin_0
  N35: R26.wiper, R27.Pin_1

custom parts:
  LuaNode32 / ESP32: New Image for LuaNode32 DOIT ESP32 DEVKIT V1. Base parts from LuaNode32 / ESP32 ESP32 based LuaNode32 by G.Noorlander DOIT Esp32 DevKit v1 (30 pins long, 11 pins width) by Werner Rothschopf (modified by vanepp Dec 2018)
